// Digital circuit RISCV.dig as structural Verilog
module RISCV (
  input  [31:0] in_1,
  input  [31:0] in_2,
  input  in_3,
  input  [31:0] in_5,
  input  [31:0] in_6,
  input  [31:0] in_8,
  input  [1:0] in_9,
  input  [31:0] in_10,
  input  [31:0] in_11,
  input  [1:0] in_12,
  input  [4:0] in_15,
  input  [4:0] in_16,
  input  in_17,
  input  in_18,
  input  [4:0] in_19,
  input  [31:0] in_20,
  input  in_23,
  input  [31:0] in_28,
  input  in_29,
  input  [31:0] in_30,
  input  [31:0] in_32,
  output [31:0] out_4,
  output [31:0] out_7,
  output out_13,
  output [31:0] out_14,
  output [31:0] out_21,
  output [31:0] out_22,
  output [6:0] out_24,
  output [4:0] out_25,
  output [4:0] out_26,
  output [4:0] out_27,
  output [31:0] out_31,
  output [31:0] out_33
);

  RAMDualPort #(.AddrBits(12), .Bits(32)) Memory ();  // open: A, Din, str, C, ld, D
  ALU #(.applicationType("GHDL")) u_ALU (.A(in_10), .B(in_11), .selector(in_12), .Zero(out_13), .Result(out_14));
  MUX_2inputs #(.applicationType("GHDL")) u_MUX_2inputs (
    .enter1(in_1), .enter2(in_2), .selector(in_3), .\output (out_4));
  MUX_3inputs #(.applicationType("GHDL")) u_MUX_3inputs (
    .enter1(in_5), .enter2(in_6), .enter3(in_8), .selector(in_9), .\output (out_7));
  splitter #(.applicationType("GHDL")) u_splitter ();  // open: address_in, address_out
  imm_gen #(.applicationType("GHDL")) u_imm_gen (.instruction(in_32), .imm_out(out_33));
  register_block #(.applicationType("GHDL")) u_register_block (
    .rg1(in_15), .rg2(in_16), .CLK(in_17), .reg_write(in_18), .rgw(in_19), .rgw_data(in_20),
    .rg1_data(out_21), .rg2_data(out_22));
  IR_block #(.applicationType("GHDL")) u_IR_block (
    .memData(in_28), .CLK(in_23), .opcode(out_24), .rs1(out_25), .rs2(out_26), .rd(out_27));
  ALU_control #(.applicationType("GHDL")) u_ALU_control ();  // open: opcode, funct3, funct7, ALUOp, selector
  reg32 #(.applicationType("GHDL")) u_reg32 (.memData(in_30), .CLK(in_29), .memOutput(out_31));
  output_control #(.applicationType("GHDL")) u_output_control ();  // open: opcode, CLK, RST, IRWrite, MemtoReg, MemWrite, MemRead, IorD, PCWrite, PCWriteCond, PCSource, ALUOp, ALUSrcB, ALUSrcA, RegWrite
endmodule

/* Code of ALU:
LIBRARY ieee;
USE ieee.std_logic_1164.all;
USE ieee.numeric_std.all;

ENTITY ALU IS
	PORT(
		A, B : IN STD_LOGIC_VECTOR(31 downto 0);
		selector : IN STD_LOGIC_VECTOR(1 downto 0);
        	Zero    : OUT STD_LOGIC;
		Result : OUT STD_LOGIC_VECTOR(31 downto 0)
	);
END ALU;

ARCHITECTURE ALU_logic OF ALU IS

	signal B_eff    : STD_LOGIC_VECTOR(31 downto 0);

	constant allZero : std_logic_vector(31 downto 0) := (others => '0');
	constant allOne : std_logic_vector(31 downto 0) := (others => '1');

    	signal Sum_ext  : UNSIGNED(32 downto 0);

    	signal Res_temp : STD_LOGIC_VECTOR(31 downto 0);
	signal and_temp : STD_LOGIC_VECTOR(31 downto 0);
	signal or_temp : STD_LOGIC_VECTOR(31 downto 0);

    	signal Cin_vec  : UNSIGNED(32 downto 0);

	BEGIN

		and_temp <= A AND B;
		or_temp <= A OR B;

------------------------------------

    B_eff <= (B xor allOne) WHEN (selector = "01") ELSE
		B;

    Cin_vec <= unsigned(allZero & selector(0));

    Sum_ext <= unsigned('0' & A) + unsigned('0' & B_eff) + Cin_vec;

    Res_temp <= std_logic_vector(Sum_ext(31 downto 0));

    Zero <= '1' WHEN ((Res_temp = allZero) AND (selector(1) = '0')) ELSE
		'0';

    Result <= and_temp WHEN (selector = "10") ELSE
		or_temp WHEN (selector = "11") ELSE
		Res_temp;

	END ALU_logic;
*/

/* Code of MUX_2inputs:
LIBRARY ieee;
USE ieee.std_logic_1164.all;

ENTITY MUX_2inputs IS
	PORT(
		enter1, enter2 : IN STD_LOGIC_VECTOR (31 downto 0);
		selector : IN STD_LOGIC;
		output : OUT STD_LOGIC_VECTOR (31 downto 0)
	);
END MUX_2inputs;

ARCHITECTURE MUX_logic OF MUX_2inputs IS
	BEGIN
		output <= enter1 WHEN selector = '0' ELSE
			enter2;

	END MUX_logic;
--------------------------------------------------------------------------------
*/

/* Code of MUX_3inputs:
LIBRARY ieee;
USE ieee.std_logic_1164.all;

ENTITY MUX_3inputs IS
	PORT(
		enter1, enter2, enter3 : IN STD_LOGIC_VECTOR (31 downto 0);
		selector: IN STD_LOGIC_VECTOR (1 downto 0);
		output : OUT STD_LOGIC_VECTOR (31 downto 0)
	);
END MUX_3inputs;

ARCHITECTURE MUX_logic OF MUX_3inputs IS
	BEGIN
		output <= enter1 WHEN selector = "00" ELSE
			enter2 WHEN selector = "01" ELSE
			enter3;

	END MUX_logic;
--------------------------------------------------------------------------------
*/

/* Code of splitter:
LIBRARY ieee;
USE ieee.std_logic_1164.all;

ENTITY splitter IS
	PORT(
		address_in : IN  STD_LOGIC_VECTOR(31 downto 0);
		address_out : OUT STD_LOGIC_VECTOR(11 downto 0)
	);
END splitter;

ARCHITECTURE behavioral OF splitter IS
BEGIN
	address_out <= address_in(13 downto 2);
END behavioral;
*/

/* Code of imm_gen:
LIBRARY ieee;
USE ieee.std_logic_1164.all;

ENTITY imm_gen IS
	PORT(
		instruction : IN  STD_LOGIC_VECTOR(31 downto 0);
		imm_out     : OUT STD_LOGIC_VECTOR(31 downto 0)
	);
END imm_gen;

ARCHITECTURE behavioral OF imm_gen IS
	ALIAS opcode : STD_LOGIC_VECTOR(6 downto 0) IS instruction(6 downto 0);
BEGIN

	PROCESS(instruction, opcode)
	BEGIN
		CASE opcode IS
			-- Tipo-I (ex: Load, addi)
			WHEN "0000011" | "0010011" =>
				imm_out <= (31 downto 12 => instruction(31)) & instruction(31 downto 20);

			-- Tipo-S (ex: Store)
			WHEN "0100011" =>
				imm_out <= (31 downto 12 => instruction(31)) & instruction(31 downto 25) & instruction(11 downto 7);

			-- Tipo-B (ex: Branch / Desvios)
			WHEN "1100011" =>
				imm_out <= (31 downto 12 => instruction(31)) & instruction(7) & instruction(30 downto 25) & instruction(11 downto 8) & '0';

			-- Padrão caso não utilize imediato
			WHEN OTHERS =>
				imm_out <= (others => '0');
		END CASE;
	END PROCESS;

END behavioral;
*/

/* Code of register_block:
LIBRARY ieee;
USE ieee.std_logic_1164.all;
USE ieee.numeric_std.all;

ENTITY register_block IS
	PORT(
		rg1, rg2 : IN STD_LOGIC_VECTOR(4 downto 0);
		CLK : IN STD_LOGIC;
		reg_write : IN STD_LOGIC;
		rgw : IN STD_LOGIC_VECTOR(4 downto 0);
		rgw_data : IN STD_LOGIC_VECTOR(31 downto 0);
		rg1_data , rg2_data : OUT STD_LOGIC_VECTOR(31 downto 0)
	);
END register_block;

ARCHITECTURE register_logic OF register_block IS

	type reg_array is array (0 to 31) of std_logic_vector(31 downto 0);
	signal registers : reg_array := (others => (others => '0'));
	signal value1 : STD_LOGIC_VECTOR(31 downto 0);
	signal value2 : STD_LOGIC_VECTOR(31 downto 0);

	BEGIN
	
		PROCESS(CLK)
			BEGIN
				IF (CLK'event AND CLK='1') THEN
					IF (reg_write = '1' AND rgw /= "00000") THEN
						registers(to_integer(unsigned(rgw))) <= rgw_data;
					END IF;
				END IF;
		END PROCESS;

		rg1_data <= registers(to_integer(unsigned(rg1)));
		rg2_data <= registers(to_integer(unsigned(rg2)));

	END register_logic;
*/

/* Code of IR_block:
LIBRARY ieee;
USE ieee.std_logic_1164.all;
USE ieee.numeric_std.all;

ENTITY IR_block IS
	PORT(
		memData : IN STD_LOGIC_VECTOR(31 downto 0);
		CLK : IN STD_LOGIC;
		opcode : OUT STD_LOGIC_VECTOR(6 downto 0);
		rs1 : OUT STD_LOGIC_VECTOR(4 downto 0);
		rs2 : OUT STD_LOGIC_VECTOR(4 downto 0);
		rd : OUT STD_LOGIC_VECTOR(4 downto 0)
	);
END IR_block;

ARCHITECTURE IR_logic OF IR_block IS
	BEGIN
	
		PROCESS(CLK)
			BEGIN
				IF (CLK'event AND CLK='1') THEN
					opcode <= memData(6 downto 0);
					rs1 <= memData(19 downto 15);
					rs2 <= memData(24 downto 20);
					rd <= memData(11 downto 7);
				ELSE
					opcode <= opcode;
					rs1 <= rs1;
					rs2 <= rs2;
					rd <= rd;
				END IF;
		END PROCESS;

	END IR_logic;
*/

/* Code of ALU_control:
LIBRARY ieee;
USE ieee.std_logic_1164.all;

ENTITY ALU_control IS
	PORT(
		opcode : IN  STD_LOGIC_VECTOR(6 downto 0);
		funct3 : IN  STD_LOGIC_VECTOR(2 downto 0);
		funct7 : IN  STD_LOGIC_VECTOR(6 downto 0);
		ALUOp  : IN STD_LOGIC_VECTOR(1 downto 0);
		selector : OUT STD_LOGIC_VECTOR(1 downto 0)
	);
END ALU_control;

ARCHITECTURE behavioral OF ALU_control IS
	
BEGIN
	PROCESS(ALUOp, opcode, funct3, funct7)
		BEGIN
			selector <= "00";
			IF(ALUOp = "00" OR opcode = "0000011" OR opcode = "0100011") THEN
				selector <= "00";
			ELSIF(ALUOp = "01" OR opcode = "1100111") THEN
				selector <= "01";
			ELSE
				IF(opcode = "0110011") THEN
					IF(funct7 = "0000000") THEN
						IF(funct3 = "000") THEN
							selector <= "00";
						ELSIF(funct3 = "111") THEN
							selector <= "10";
						ELSIF(funct3 = "110") THEN
							selector <= "11";
						END IF;
					ELSIF(funct7 = "0100000") THEN
						selector <= "01";
					END IF;
				END IF;
			END IF;
		END PROCESS;
END behavioral;
*/

/* Code of reg32:
LIBRARY ieee;
USE ieee.std_logic_1164.all;
USE ieee.numeric_std.all;

ENTITY reg32 IS
	PORT(
		memData : IN STD_LOGIC_VECTOR(31 downto 0);
		CLK : IN STD_LOGIC;
		memOutput : OUT STD_LOGIC_VECTOR(31 downto 0)
	);
END reg32;

ARCHITECTURE reg32_logic OF reg32 IS
	BEGIN
	
		PROCESS(CLK)
			BEGIN
				IF (CLK'event AND CLK='1') THEN
					memOutput <= memData;
				ELSE
					memOutput <= memOutput;
				END IF;
		END PROCESS;

	END reg32_logic;
*/

/* Code of output_control:
LIBRARY ieee;
USE ieee.std_logic_1164.all;
USE ieee.numeric_std.all;

ENTITY output_control IS
	PORT(
		opcode : IN STD_LOGIC_VECTOR(6 downto 0);
		CLK : IN STD_LOGIC;
		RST : IN STD_LOGIC;
		IRWrite : OUT STD_LOGIC;
		MemtoReg : OUT STD_LOGIC;
		MemWrite : OUT STD_LOGIC;
		MemRead : OUT STD_LOGIC;
		IorD : OUT STD_LOGIC;
		PCWrite : OUT STD_LOGIC;
		PCWriteCond : OUT STD_LOGIC;
		PCSource : OUT STD_LOGIC;
		ALUOp : OUT STD_LOGIC_VECTOR (1 downto 0);
		ALUSrcB : OUT STD_LOGIC_VECTOR (1 downto 0);
		ALUSrcA : OUT STD_LOGIC;
		RegWrite : OUT STD_LOGIC
	);
END output_control;

ARCHITECTURE output_control_logic OF output_control IS

	CONSTANT opAritmetica : STD_LOGIC_VECTOR(6 downto 0) := "0110011";
	CONSTANT LW : STD_LOGIC_VECTOR(6 downto 0) := "0000011";
	CONSTANT SW : STD_LOGIC_VECTOR(6 downto 0) := "0100011";
	CONSTANT BRANCH : STD_LOGIC_VECTOR(6 downto 0) := "1100111";

	TYPE state_type IS (s_fetch, s_decode, s_addressComp, s_MemoryAccessLoad, s_MemoryAccessStore, s_MemoryReadLoad, 
	s_Execution, s_RtypeComp, s_Branch);

	SIGNAL state_next : state_type;
	SIGNAL state_reg : state_type := s_fetch;

	BEGIN
	PROCESS(clk)
		BEGIN
			IF RST = '1' THEN
				state_reg <= s_fetch;
			ELSIF rising_edge(CLK) THEN
				state_reg <= state_next;
			END IF;
		END PROCESS;

	PROCESS(state_reg, opcode)
		BEGIN
			CASE state_reg IS
				WHEN s_fetch =>
					state_next <= s_decode;

				WHEN s_decode =>
					IF opcode = LW OR opcode = SW THEN
						state_next <= s_addressComp;
					ELSIF opcode = opAritmetica THEN
						state_next <= s_Execution;
					ELSIF opcode = BRANCH THEN
						state_next <= s_Branch;
					ELSE
						state_next <= s_fetch; -- Opcode desconhecido reinicia a busca
					END IF;

				WHEN s_addressComp =>
					IF opcode = LW THEN
						state_next <= s_MemoryAccessLoad;
					ELSIF opcode = SW THEN
						state_next <= s_MemoryAccessStore;
					ELSE
						state_next <= s_fetch;
					END IF;

				WHEN s_MemoryAccessLoad =>
					state_next <= s_MemoryReadLoad;

				WHEN s_MemoryReadLoad | s_MemoryAccessStore | s_RtypeComp | s_Branch =>
					state_next <= s_fetch;

				WHEN s_Execution =>
					state_next <= s_RtypeComp;

				WHEN OTHERS =>
					state_next <= s_fetch;
			END CASE;
		END PROCESS;
				

		PROCESS(state_reg)
		BEGIN
			IRWrite     <= '0';
			MemtoReg    <= '0';
			MemWrite    <= '0';
			MemRead     <= '0';
			IorD        <= '0';
			PCWrite     <= '0';
			PCWriteCond <= '0';
			PCSource    <= '0';
			ALUOp       <= "00";
			ALUSrcB     <= "00";
			ALUSrcA     <= '0';
			RegWrite    <= '0';
			CASE state_reg IS
				WHEN s_fetch =>
					MemRead <= '1';
					ALUSrcA <= '0';
					IorD <= '0';
					IRWrite <= '1';
					ALUSrcB <= "01";
					ALUOp <= "00";
					PCWrite <= '1';
					PCSource <= '0';
				WHEN s_decode =>
					ALUSrcA <= '0';
					ALUSrcB <= "10";
					ALUOp <= "00";
				WHEN s_addressComp =>
					ALUSrcA <= '1';
					ALUSrcB <= "10";
					ALUOp <= "00";
				WHEN s_MemoryAccessLoad =>
					MemRead <= '1';
					IorD <= '1';
				WHEN s_MemoryReadLoad =>
					RegWrite <= '1';
					MemtoReg <= '1';
				WHEN s_MemoryAccessStore =>
					MemWrite <= '1';
					IorD <= '1';
				WHEN s_Execution =>
					ALUSrcA <= '1';
					ALUSrcB <= "00";
					ALUOp <= "10";
				WHEN s_RtypeComp =>
					RegWrite <= '1';
					MemtoReg <= '0';
				WHEN s_Branch =>
					ALUSrcA <= '1';
					ALUSrcB <= "00";
					ALUOp <= "01";
					PCWriteCond <= '1';
					PCSource <= '1';
				END CASE;
			END PROCESS;
	END output_control_logic;
*/
